// Logisim project mini-calc.circ as structural Verilog: 3 circuits, main circuit main
module main (
  input  in_1,
  input  in_2,
  input  in_3,
  input  in_4,
  input  in_5,
  input  in_6,
  input  in_7,
  input  in_8,
  output out_9,
  output out_10,
  output out_11,
  output out_12,
  output out_13
);

  wire fulladder_1_x, fulladder_2_x, hafladder_1_out_3;

  Hafladder hafladder_1 (.in_1(in_4), .in_2(in_8), .out_3(hafladder_1_out_3), .out_4(out_13));
  Fulladder fulladder_1 (.a(in_3), .x(fulladder_1_x), .b(in_7), .y(out_12), .c(hafladder_1_out_3));
  Fulladder fulladder_2 (.a(in_2), .x(fulladder_2_x), .b(in_6), .y(out_11), .c(fulladder_1_x));
  Fulladder fulladder_3 (.a(in_1), .x(out_9), .b(in_5), .y(out_10), .c(fulladder_2_x));

  // Notes on the sheet:
  //   10 + 10 = 1010 + 1010 = 20 =
  //   10100
endmodule

module Fulladder (
  input  a,
  input  b,
  input  c,
  output x,
  output y
);

  wire and_1_out, and_2_out, xor_1_out;

  and and_1 (and_1_out, a, b);
  xor xor_1 (xor_1_out, a, b);
  and and_2 (and_2_out, xor_1_out, c);
  or or_1 (x, and_1_out, and_2_out);
  xor xor_2 (y, xor_1_out, c);
endmodule

module Hafladder (
  input  in_1,
  input  in_2,
  output out_3,
  output out_4
);

  and and_1 (out_3, in_1, in_2);
  xor xor_1 (out_4, in_1, in_2);
endmodule
